# Fritzing sketch Battery Check (saved by Fritzing 0.9.3b)
circuit board: 5.12953cm x 5.08656cm
breadboards: 1

parts:
  Voltimetter = Adafruit ADS1115 16Bit I2C ADC [part_number="Adafruit 1115"]
  R1 = Resistor [tolerance=±5% resistance=0.8 package=THT]
  Battery = Lithium Ion Cylindrical Battery 3.7v 2200mAh [part_number=18650]
  R2 = Resistor [tolerance=±5% resistance=3.3 package=THT]
  Arduino = Arduino Nano (Rev3.0)

nets:
  N1: Voltimetter.AIN1, R1.Pin_0, R2.Pin_1
  N2: Voltimetter.AIN0, R1.Pin_1, Battery.positive
  GND: Voltimetter.ADDR, Voltimetter.GND, Battery.negative, R2.Pin_0, Arduino.GND
  N3: Voltimetter.SDA, Arduino.A4
  N4: Voltimetter.SCL, Arduino.A5
  VDD: Voltimetter.VDD, Arduino.5V

custom parts:
  Adafruit ADS1115 16Bit I2C ADC: For microcontrollers without an analog-to-digital converter or when you want a higher-precision ADC, the ADS1115 provides 16-bit precision at 860 samples/second over I2C. The chip can be configured as 4 single-ended input channels, or two differential channels. As a nice bonus, it even includes a programmable gain amplifier, up to x16, to help boost up smaller single/differential signals to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
  Lithium Ion Cylindrical Battery 3.7v 2200mAh: This lithium ion battery has a capacity of 2200mAh and a protection circuit that provides over-voltage, under-voltage and over-current protection. This cell can provide 2C of peak current (4400mA). Note that these batteries are not designed to sustain such high loads, we suggest keeping any constant current draw under about 0.5C (1 Amp).
